# Fritzing sketch Carte4x8Input24Vj (saved by Fritzing 0.9.2b)
circuit board: 9.9cm x 8.2cm
breadboards: 2

parts:
  IN1 = 74HC165 [part_number=SN74LS165 package="DIP16 [THT]"]
  IN2 = 74HC165 [part_number=SN74LS165 package="DIP16 [THT]"]
  IN3 = 74HC165 [part_number=SN74LS165 package="DIP16 [THT]"]
  IN4 = 74HC165 [part_number=SN74LS165 package="DIP16 [THT]"]
  PL_CE_DS_CP_1 = female pin header, 4 pins [form="♀ (female)"]
  PL_CE_DS_CP_2 = female pin header, 4 pins [form="♀ (female)"]
  VCC_GND = female pin header, 2 pins [form="♀ (female)"]
  VCC_GND1 = female pin header, 2 pins [form="♀ (female)"]
  INPUT1 = female pin header, 8 pins [form="♀ (female)"]
  R15 = Resistor [tolerance=±5% resistance=47k package=THT]
  R16 = Resistor [tolerance=±5% resistance=10k package=THT]
  R17 = Resistor [tolerance=±5% resistance=10k package=THT]
  R18 = Resistor [tolerance=±5% resistance=10k package=THT]
  R19 = Resistor [tolerance=±5% resistance=10k package=THT]
  R20 = Resistor [tolerance=±5% resistance=10k package=THT]
  R21 = Resistor [tolerance=±5% resistance=10k package=THT]
  R22 = Resistor [tolerance=±5% resistance=10k package=THT]
  R23 = Resistor [tolerance=±5% resistance=10k package=THT]
  R24 = Resistor [tolerance=±5% resistance=10k package=THT]
  R25 = Resistor [tolerance=±5% resistance=10k package=THT]
  R26 = Resistor [tolerance=±5% resistance=10k package=THT]
  R27 = Resistor [tolerance=±5% resistance=10k package=THT]
  R28 = Resistor [tolerance=±5% resistance=10k package=THT]
  R29 = Resistor [tolerance=±5% resistance=10k package=THT]
  R30 = Resistor [tolerance=±5% resistance=10k package=THT]
  R31 = Resistor [tolerance=±5% resistance=10k package=THT]
  R32 = Resistor [tolerance=±5% resistance=10k package=THT]
  R33 = Resistor [tolerance=±5% resistance=10k package=THT]
  R34 = Resistor [tolerance=±5% resistance=10k package=THT]
  R35 = Resistor [tolerance=±5% resistance=10k package=THT]
  R36 = Resistor [tolerance=±5% resistance=10k package=THT]
  R37 = Resistor [tolerance=±5% resistance=10k package=THT]
  R38 = Resistor [tolerance=±5% resistance=10k package=THT]
  R39 = Resistor [tolerance=±5% resistance=10k package=THT]
  R40 = Resistor [tolerance=±5% resistance=10k package=THT]
  R41 = Resistor [tolerance=±5% resistance=10k package=THT]
  R42 = Resistor [tolerance=±5% resistance=10k package=THT]
  R43 = Resistor [tolerance=±5% resistance=10k package=THT]
  R44 = Resistor [tolerance=±5% resistance=10k package=THT]
  R45 = Resistor [tolerance=±5% resistance=10k package=THT]
  R46 = Resistor [tolerance=±5% resistance=10k package=THT]
  R47 = Resistor [tolerance=±5% resistance=10k package=THT]
  R48 = Resistor [tolerance=±5% resistance=47k package=THT]
  R49 = Resistor [tolerance=±5% resistance=47k package=THT]
  R50 = Resistor [tolerance=±5% resistance=47k package=THT]
  R51 = Resistor [tolerance=±5% resistance=47k package=THT]
  R52 = Resistor [tolerance=±5% resistance=47k package=THT]
  R53 = Resistor [tolerance=±5% resistance=47k package=THT]
  R54 = Resistor [tolerance=±5% resistance=47k package=THT]
  R55 = Resistor [tolerance=±5% resistance=47k package=THT]
  R56 = Resistor [tolerance=±5% resistance=47k package=THT]
  R57 = Resistor [tolerance=±5% resistance=47k package=THT]
  R58 = Resistor [tolerance=±5% resistance=47k package=THT]
  R59 = Resistor [tolerance=±5% resistance=47k package=THT]
  R60 = Resistor [tolerance=±5% resistance=47k package=THT]
  R61 = Resistor [tolerance=±5% resistance=47k package=THT]
  R62 = Resistor [tolerance=±5% resistance=47k package=THT]
  R63 = Resistor [tolerance=±5% resistance=47k package=THT]
  R64 = Resistor [tolerance=±5% resistance=47k package=THT]
  R65 = Resistor [tolerance=±5% resistance=47k package=THT]
  R66 = Resistor [tolerance=±5% resistance=47k package=THT]
  R67 = Resistor [tolerance=±5% resistance=47k package=THT]
  R68 = Resistor [tolerance=±5% resistance=47k package=THT]
  R69 = Resistor [tolerance=±5% resistance=47k package=THT]
  R70 = Resistor [tolerance=±5% resistance=47k package=THT]
  R71 = Resistor [tolerance=±5% resistance=47k package=THT]
  R72 = Resistor [tolerance=±5% resistance=47k package=THT]
  R73 = Resistor [tolerance=±5% resistance=47k package=THT]
  R74 = Resistor [tolerance=±5% resistance=47k package=THT]
  R75 = Resistor [tolerance=±5% resistance=47k package=THT]
  R76 = Resistor [tolerance=±5% resistance=47k package=THT]
  R77 = Resistor [tolerance=±5% resistance=47k package=THT]
  R78 = Resistor [tolerance=±5% resistance=47k package=THT]
  INPUT2 = female pin header, 8 pins [form="♀ (female)"]
  INPUT3 = female pin header, 8 pins [form="♀ (female)"]
  INPUT4 = female pin header, 8 pins [form="♀ (female)"]
  INPUT1b = female pin header, 8 pins [form="♀ (female)"]
  INPUT2b = female pin header, 8 pins [form="♀ (female)"]
  INPUT3b = female pin header, 8 pins [form="♀ (female)"]
  INPUT4b = female pin header, 8 pins [form="♀ (female)"]

nets:
  N1: IN1.PL, IN2.PL, IN3.PL, IN4.PL, PL_CE_DS_CP_1.pin1, PL_CE_DS_CP_2.pin1
  N2: IN1.CP, IN2.CP, IN3.CP, IN4.CP, PL_CE_DS_CP_1.pin4, PL_CE_DS_CP_2.pin4
  N3: IN1.D4, R41.Pin_0, R73.Pin_1
  N4: IN1.D5, R47.Pin_0, R71.Pin_1
  N5: IN1.D6, R46.Pin_0, R74.Pin_1
  N6: IN1.D7, R45.Pin_0, R75.Pin_1
  GND: IN1.GND, IN2.GND, IN3.GND, IN4.GND, IN4.DS, VCC_GND.pin2, VCC_GND1.pin2, R16.Pin_1, R17.Pin_1, R18.Pin_1, R19.Pin_1, R20.Pin_1, R21.Pin_1, R22.Pin_1, R23.Pin_1, R24.Pin_1, R25.Pin_1, R26.Pin_1, R27.Pin_1, R28.Pin_1, R29.Pin_1, R30.Pin_1, R31.Pin_1, R32.Pin_1, R33.Pin_1, R34.Pin_1, R35.Pin_1, R36.Pin_1, R37.Pin_1, R38.Pin_1, R39.Pin_1, R40.Pin_1, R41.Pin_1, R42.Pin_1, R43.Pin_1, R44.Pin_1, R45.Pin_1, R46.Pin_1, R47.Pin_1
  N7: IN1.Q7, PL_CE_DS_CP_1.pin3, PL_CE_DS_CP_2.pin3
  N8: IN1.DS, IN2.Q7
  N9: IN1.D0, R40.Pin_0, R78.Pin_1
  N10: IN1.D1, R44.Pin_0, R72.Pin_1
  N11: IN1.D2, R43.Pin_0, R77.Pin_1
  N12: IN1.D3, R42.Pin_0, R76.Pin_1
  N13: IN1.CE, IN2.CE, IN3.CE, IN4.CE, PL_CE_DS_CP_1.pin2, PL_CE_DS_CP_2.pin2
  VCC: IN1.VCC, IN2.VCC, IN3.VCC, IN4.VCC, VCC_GND.pin1, VCC_GND1.pin1
  N14: IN2.D4, R36.Pin_0, R63.Pin_1
  N15: IN2.D5, R38.Pin_0, R70.Pin_1
  N16: IN2.D6, R35.Pin_0, R67.Pin_1
  N17: IN2.D7, R33.Pin_0, R64.Pin_1
  N18: IN2.DS, IN3.Q7
  N19: IN2.D0, R32.Pin_0, R65.Pin_1
  N20: IN2.D1, R39.Pin_0, R69.Pin_1
  N21: IN2.D2, R37.Pin_0, R66.Pin_1
  N22: IN2.D3, R34.Pin_0, R68.Pin_1
  N23: IN3.D4, R26.Pin_0, R62.Pin_1
  N24: IN3.D5, R28.Pin_0, R59.Pin_1
  N25: IN3.D6, R27.Pin_0, R61.Pin_1
  N26: IN3.D7, R31.Pin_0, R60.Pin_1
  N27: IN3.DS, IN4.Q7
  N28: IN3.D0, R24.Pin_0, R55.Pin_1
  N29: IN3.D1, R30.Pin_0, R56.Pin_1
  N30: IN3.D2, R25.Pin_0, R57.Pin_1
  N31: IN3.D3, R29.Pin_0, R58.Pin_1
  N32: IN4.D4, R20.Pin_0, R51.Pin_1
  N33: IN4.D5, R23.Pin_0, R52.Pin_1
  N34: IN4.D6, R21.Pin_0, R53.Pin_1
  N35: IN4.D7, R22.Pin_0, R54.Pin_1
  N36: IN4.D0, R15.Pin_1, R16.Pin_0
  N37: IN4.D1, R17.Pin_0, R48.Pin_1
  N38: IN4.D2, R18.Pin_0, R49.Pin_1
  N39: IN4.D3, R19.Pin_0, R50.Pin_1
  N40: INPUT1.pin1, R54.Pin_0, INPUT1b.pin1
  N41: INPUT1.pin2, R53.Pin_0, INPUT1b.pin2
  N42: INPUT1.pin3, R52.Pin_0, INPUT1b.pin3
  N43: INPUT1.pin4, R51.Pin_0, INPUT1b.pin4
  N44: INPUT1.pin5, R50.Pin_0, INPUT1b.pin5
  N45: INPUT1.pin6, R49.Pin_0, INPUT1b.pin6
  N46: INPUT1.pin7, R48.Pin_0, INPUT1b.pin7
  N47: INPUT1.pin8, R15.Pin_0, INPUT1b.pin8
  N48: R55.Pin_0, INPUT2.pin8, INPUT2b.pin8
  N49: R56.Pin_0, INPUT2.pin7, INPUT2b.pin7
  N50: R57.Pin_0, INPUT2.pin6, INPUT2b.pin6
  N51: R58.Pin_0, INPUT2.pin5, INPUT2b.pin5
  N52: R59.Pin_0, INPUT2.pin3, INPUT2b.pin3
  N53: R60.Pin_0, INPUT2.pin1, INPUT2b.pin1
  N54: R61.Pin_0, INPUT2.pin2, INPUT2b.pin2
  N55: R62.Pin_0, INPUT2.pin4, INPUT2b.pin4
  N56: R63.Pin_0, INPUT3.pin4, INPUT3b.pin4
  N57: R64.Pin_0, INPUT3.pin1, INPUT3b.pin1
  N58: R65.Pin_0, INPUT3.pin8, INPUT3b.pin8
  N59: R66.Pin_0, INPUT3.pin6, INPUT3b.pin6
  N60: R67.Pin_0, INPUT3.pin2, INPUT3b.pin2
  N61: R68.Pin_0, INPUT3.pin5, INPUT3b.pin5
  N62: R69.Pin_0, INPUT3.pin7, INPUT3b.pin7
  N63: R70.Pin_0, INPUT3.pin3, INPUT3b.pin3
  N64: R71.Pin_0, INPUT4.pin3, INPUT4b.pin3
  N65: R72.Pin_0, INPUT4.pin7, INPUT4b.pin7
  N66: R73.Pin_0, INPUT4.pin4, INPUT4b.pin4
  N67: R74.Pin_0, INPUT4.pin2, INPUT4b.pin2
  N68: R75.Pin_0, INPUT4.pin1, INPUT4b.pin1
  N69: R76.Pin_0, INPUT4.pin5, INPUT4b.pin5
  N70: R77.Pin_0, INPUT4.pin6, INPUT4b.pin6
  N71: R78.Pin_0, INPUT4.pin8, INPUT4b.pin8

notes:
  31 30 29 28 27 26 25 24
  23 22 21 20 19 18 17 16
  08 09 10 11 12 13 14 15
  0 1 2 3 4 5 6 7
  |
  3
  1
  +5V
  2
  4
  GND
  PL CE DS CP
  32 INPUT 24V V0.1

custom parts:
  74HC165: 8-bit parallel-load shift registers
