# Fritzing sketch Carte4x8Outputs24Vj (saved by Fritzing 0.9.2b)
circuit board: 9.9cm x 8.2cm
breadboards: 4

parts:
  Q1 = ULN2803 Darlington Array
  U1 = 74HC595 [package="DIP16 [THT]"]
  U2 = 74HC595 [package="DIP16 [THT]"]
  Q2 = ULN2803 Darlington Array
  J1 = female pin header, 8 pins [form="♀ (female)"]
  J2 = female pin header, 8 pins [form="♀ (female)"]
  J3 = female pin header, 8 pins [form="♀ (female)"]
  J4 = female pin header, 8 pins [form="♀ (female)"]
  J5V = female pin header, 2 pins [form="♀ (female)"]
  J24V = female pin header, 2 pins [form="♀ (female)"]
  JDLC = female pin header, 3 pins [form="♀ (female)"]
  DT_LT_CLK = female pin header, 3 pins [form="♀ (female)"]
  5V = female pin header, 2 pins [form="♀ (female)"]
  24V = female pin header, 2 pins [form="♀ (female)"]
  J5 = female pin header, 8 pins [form="♀ (female)"]
  Q3 = ULN2803 Darlington Array
  U3 = 74HC595 [package="DIP16 [THT]"]
  J6 = female pin header, 8 pins [form="♀ (female)"]
  J7 = female pin header, 8 pins [form="♀ (female)"]
  J8 = female pin header, 8 pins [form="♀ (female)"]
  Q4 = ULN2803 Darlington Array
  U4 = 74HC595 [package="DIP16 [THT]"]
  J_0V = female pin header, 2 pins [form="♀ (female)"]
  0V = female pin header, 2 pins [form="♀ (female)"]

nets:
  N1: Q1.I1, U1.Q7
  N2: Q1.I2, U1.Q6
  N3: Q1.I3, U1.Q5
  N4: Q1.I4, U1.Q4
  N5: Q1.I5, U1.Q3
  N6: Q1.I6, U1.Q2
  N7: Q1.I7, U1.Q1
  N8: Q1.I8, U1.Q0
  N9: Q1.COMMON, Q2.COMMON, J24V.pin1, J24V.pin2, 24V.pin1, 24V.pin2, Q3.COMMON, Q4.COMMON
  GND: Q1.GND, U1.GND, U1.OE, U2.GND, U2.OE, Q2.GND, Q3.GND, U3.GND, U3.OE, Q4.GND, U4.GND, U4.OE, J_0V.pin1, J_0V.pin2, 0V.pin1, 0V.pin2
  N10: Q1.O8, J1.pin8, J2.pin8
  N11: Q1.O7, J1.pin7, J2.pin7
  N12: Q1.O6, J1.pin6, J2.pin6
  N13: Q1.O5, J1.pin5, J2.pin5
  N14: Q1.O4, J1.pin4, J2.pin4
  N15: Q1.O3, J1.pin3, J2.pin3
  N16: Q1.O2, J1.pin2, J2.pin2
  N17: Q1.O1, J1.pin1, J2.pin1
  N18: U1.Q7', U2.DS
  VCC: U1.MR, U1.VCC, U2.MR, U2.VCC, J5V.pin1, J5V.pin2, 5V.pin1, 5V.pin2, U3.MR, U3.VCC, U4.MR, U4.VCC
  N19: U1.SH_CP, U2.SH_CP, JDLC.pin3, DT_LT_CLK.pin3, U3.SH_CP, U4.SH_CP
  N20: U1.ST_CP, U2.ST_CP, JDLC.pin2, DT_LT_CLK.pin2, U3.ST_CP, U4.ST_CP
  N21: U1.DS, JDLC.pin1, DT_LT_CLK.pin1
  N22: U2.Q1, Q2.I7
  N23: U2.Q2, Q2.I6
  N24: U2.Q3, Q2.I5
  N25: U2.Q4, Q2.I4
  N26: U2.Q5, Q2.I3
  N27: U2.Q6, Q2.I2
  N28: U2.Q7, Q2.I1
  N29: U2.Q7', U3.DS
  N30: U2.Q0, Q2.I8
  N31: Q2.O8, J3.pin8, J4.pin8
  N32: Q2.O7, J3.pin7, J4.pin7
  N33: Q2.O6, J3.pin6, J4.pin6
  N34: Q2.O5, J3.pin5, J4.pin5
  N35: Q2.O4, J3.pin4, J4.pin4
  N36: Q2.O3, J3.pin3, J4.pin3
  N37: Q2.O2, J3.pin2, J4.pin2
  N38: Q2.O1, J3.pin1, J4.pin1
  N39: J5.pin1, Q3.O1, J6.pin1
  N40: J5.pin2, Q3.O2, J6.pin2
  N41: J5.pin3, Q3.O3, J6.pin3
  N42: J5.pin4, Q3.O4, J6.pin4
  N43: J5.pin5, Q3.O5, J6.pin5
  N44: J5.pin6, Q3.O6, J6.pin6
  N45: J5.pin7, Q3.O7, J6.pin7
  N46: J5.pin8, Q3.O8, J6.pin8
  N47: Q3.I1, U3.Q7
  N48: Q3.I2, U3.Q6
  N49: Q3.I3, U3.Q5
  N50: Q3.I4, U3.Q4
  N51: Q3.I5, U3.Q3
  N52: Q3.I6, U3.Q2
  N53: Q3.I7, U3.Q1
  N54: Q3.I8, U3.Q0
  N55: U3.Q7', U4.DS
  N56: J7.pin1, J8.pin1, Q4.O1
  N57: J7.pin2, J8.pin2, Q4.O2
  N58: J7.pin3, J8.pin3, Q4.O3
  N59: J7.pin4, J8.pin4, Q4.O4
  N60: J7.pin5, J8.pin5, Q4.O5
  N61: J7.pin6, J8.pin6, Q4.O6
  N62: J7.pin7, J8.pin7, Q4.O7
  N63: J7.pin8, J8.pin8, Q4.O8
  N64: Q4.I1, U4.Q7
  N65: Q4.I2, U4.Q6
  N66: Q4.I3, U4.Q5
  N67: Q4.I4, U4.Q4
  N68: Q4.I5, U4.Q3
  N69: Q4.I6, U4.Q2
  N70: Q4.I7, U4.Q1
  N71: Q4.I8, U4.Q0

notes:
  0 1 2 3 4 5 6 7
  08 09 10 11 12 13 14 15
  23 22 21 20 19 18 17 16
  24V
  5V
  31 30 29 28 27 26 25 24
  |
  DT LT CLK
  ULN2803
  74HC595
  32 OUTPUT REV 0.3
  1
  2
  3
  4
  GND
  Data
  Latch
  Clock
  Output power
  0V

custom parts:
  ULN2803 Darlington Array: ULN2803 Darlington Transistor Array with Flyback Protection
